# Fritzing sketch 3prototipo (saved by Fritzing 0.9.3b)

parts:
  Componente1 = ESP12E Motor Shield
  U1 = NodeMCU V1.0
  M2 = fc-51 [package=THT]
  M3 = fc-51 [package=THT]
  M4 = fc-51 [package=THT]
  M5 = DC Motor
  M6 = DC Motor
  BAT1 = BC9VPC [package=bc9vpc]
  BAT2 = BC9VPC [package=bc9vpc]

nets:
  N1: Componente1.D0#0, M2.pin1
  N2: Componente1.D1, Componente1.G#6, Componente1.D6#8, Componente1.D7#9, M2.pin2, M3.pin1
  N3: Componente1.3V3#5, M2.pin3
  N4: Componente1.3V3#19, Componente1.3V3#47, Componente1.3V3#54, U1.3V3
  N5: Componente1.G#33, Componente1.G#44, Componente1.G#48, Componente1.G#55, U1.GND
  N6: Componente1.SD0, U1.SD0
  N7: Componente1.CMD, U1.CMD
  N8: Componente1.SD1, U1.SD1
  N9: Componente1.SD2#38, M4.pin1
  N10: Componente1.RSV#40, U1.RSV#40
  N11: Componente1.VIN#43, U1.Vin
  N12: Componente1.RST, U1.RST
  N13: Componente1.EN, U1.EN
  N14: Componente1.CLK, U1.CLK
  N15: Componente1.SD2#50, U1.SD2
  N16: Componente1.SD3, U1.SD3
  N17: Componente1.RSV#52, U1.RSV#41
  N18: Componente1.AD0, U1.A0
  N19: Componente1.TX, U1.TX
  N20: Componente1.RX, U1.RX
  N21: Componente1.D8, U1.D8
  N22: Componente1.D7#59, U1.D7
  N23: Componente1.D6#60, U1.D6
  N24: Componente1.D5, U1.D5
  N25: Componente1.CB, U1.D4
  N26: Componente1.DA, U1.D3
  N27: Componente1.PWMB, U1.D2
  N28: Componente1.PWMA, U1.D1
  N29: Componente1.D0#66, U1.D0
  N30: Componente1.V#76, M4.pin3
  N31: Componente1.V#79, M3.pin3
  N32: Componente1.G#86, M4.pin2
  N33: Componente1.G#89, M3.pin2
  N34: Componente1.A-, M6.pin_2
  N35: Componente1.A+, M6.pin_1
  N36: Componente1.B-, M5.pin_1
  N37: Componente1.B+, M5.pin_2
  N38: Componente1.VM, BAT1.V+
  N39: Componente1.GND#101, BAT1.V-
  N40: Componente1.VIN#102, BAT2.V+
  N41: Componente1.GND#103, BAT2.V-

custom parts:
  ESP12E Motor Shield: ESP8266 WiFi Motor Drive Expansion Board For NodeMCU ESP-12E
  NodeMCU V1.0: ESP8266 based NodeMCU
