# Fritzing sketch 4prototipo (saved by Fritzing 0.9.3b)

parts:
  Componente2 = ESP12E Motor Shield
  U2 = NodeMCU V1.0
  M7 = fc-51 [package=THT]
  M8 = fc-51 [package=THT]
  M9 = fc-51 [package=THT]
  M10 = DC Motor
  M11 = DC Motor
  BAT3 = BC9VPC [package=bc9vpc]
  BAT4 = BC9VPC [package=bc9vpc]
  GY1 = MPU-6050 Board GY-521 [form="♀ (female)" package=THT]

nets:
  N1: Componente2.D0#0, M7.pin1
  N2: Componente2.D1, Componente2.G#6, Componente2.D5#7, Componente2.D6#8, Componente2.D7#9, M7.pin2, M8.pin1, GY1.pin3, GY1.pin4
  N3: Componente2.3V3#5, M7.pin3
  N4: Componente2.Vin, GY1.pin1
  N5: Componente2.GND#16, GY1.pin2
  N6: Componente2.3V3#19, Componente2.3V3#47, Componente2.3V3#54, U2.3V3
  N7: Componente2.G#33, Componente2.G#44, Componente2.G#48, Componente2.G#55, U2.GND
  N8: Componente2.SD0, U2.SD0
  N9: Componente2.CMD, U2.CMD
  N10: Componente2.SD1, U2.SD1
  N11: Componente2.SD2#38, M9.pin1
  N12: Componente2.RSV#40, U2.RSV#40
  N13: Componente2.VIN#43, U2.Vin
  N14: Componente2.RST, U2.RST
  N15: Componente2.EN, U2.EN
  N16: Componente2.CLK, U2.CLK
  N17: Componente2.SD2#50, U2.SD2
  N18: Componente2.SD3, U2.SD3
  N19: Componente2.RSV#52, U2.RSV#41
  N20: Componente2.AD0, U2.A0
  N21: Componente2.TX, U2.TX
  N22: Componente2.RX, U2.RX
  N23: Componente2.D8, U2.D8
  N24: Componente2.D7#59, U2.D7
  N25: Componente2.D6#60, U2.D6
  N26: Componente2.D5#61, U2.D5
  N27: Componente2.CB, U2.D4
  N28: Componente2.DA, U2.D3
  N29: Componente2.PWMB, U2.D2
  N30: Componente2.PWMA, U2.D1
  N31: Componente2.D0#66, U2.D0
  N32: Componente2.V#76, M9.pin3
  N33: Componente2.V#79, M8.pin3
  N34: Componente2.G#86, M9.pin2
  N35: Componente2.G#89, M8.pin2
  N36: Componente2.A-, M11.pin_2
  N37: Componente2.A+, M11.pin_1
  N38: Componente2.B-, M10.pin_1
  N39: Componente2.B+, M10.pin_2
  N40: Componente2.VM, BAT3.V+
  N41: Componente2.GND#101, BAT3.V-
  N42: Componente2.VIN#102, BAT4.V+
  N43: Componente2.GND#103, BAT4.V-

custom parts:
  ESP12E Motor Shield: ESP8266 WiFi Motor Drive Expansion Board For NodeMCU ESP-12E
  NodeMCU V1.0: ESP8266 based NodeMCU
  MPU-6050 Board GY-521: Acelerometro y Giroscopio MPU-6050 Board GY-521
