# Fritzing sketch motorEsensor (saved by Fritzing 0.9.3b)

parts:
  Componente1 = ESP12E Motor Shield
  U1 = NodeMCU V1.0
  M1 = fc-51 [package=THT]
  VCC1 = Battery block 9V
  VCC2 = Battery block 9V
  M2 = DC Motor
  M3 = DC Motor

nets:
  N1: Componente1.D1, Componente1.D5#7, Componente1.3V3#14, M1.pin1
  N2: Componente1.RST#17, Componente1.3V3#19, Componente1.3V3#47, Componente1.3V3#54, U1.3V3
  N3: Componente1.G#33, Componente1.G#44, Componente1.G#48, Componente1.G#55, U1.GND
  N4: Componente1.SD0, U1.SD0
  N5: Componente1.CMD, U1.CMD
  N6: Componente1.SD1, U1.SD1
  N7: Componente1.RSV#40, U1.RSV#40
  N8: Componente1.VIN#43, U1.Vin
  N9: Componente1.RST#45, U1.RST
  N10: Componente1.EN, U1.EN
  N11: Componente1.CLK, U1.CLK
  N12: Componente1.SD2, U1.SD2
  N13: Componente1.SD3, U1.SD3
  N14: Componente1.RSV#52, U1.RSV#41
  N15: Componente1.AD0, U1.A0
  N16: Componente1.TX, U1.TX
  N17: Componente1.RX, U1.RX
  N18: Componente1.D8, U1.D8
  N19: Componente1.D7, U1.D7
  N20: Componente1.D6, U1.D6
  N21: Componente1.D5#61, U1.D5
  N22: Componente1.CB, U1.D4
  N23: Componente1.DA, U1.D3
  N24: Componente1.PWMB, U1.D2
  N25: Componente1.PWMA, U1.D1
  N26: Componente1.D0, U1.D0
  N27: Componente1.V, M1.pin2
  N28: Componente1.G#91, M1.pin3
  N29: Componente1.A-, M3.pin_2
  N30: Componente1.A+, M3.pin_1
  N31: Componente1.B-, M2.pin_2
  N32: Componente1.B+, M2.pin_1
  N33: Componente1.VM, VCC1.+
  N34: Componente1.GND#101, VCC1.-
  N35: Componente1.VIN#102, VCC2.+
  N36: Componente1.GND#103, VCC2.-

custom parts:
  ESP12E Motor Shield: ESP8266 WiFi Motor Drive Expansion Board For NodeMCU ESP-12E
  NodeMCU V1.0: ESP8266 based NodeMCU
