# Fritzing sketch MotoresH (saved by Fritzing 0.9.3b)

parts:
  Componente1 = ESP12E Motor Shield
  U1 = NodeMCU V1.0
  M1 = DC Motor
  M2 = DC Motor
  VCC1 = Battery block 9V
  VCC2 = Battery block 9V

nets:
  3V3: Componente1.3V3, U1.3V3
  N1: Componente1.G, U1.GND
  N2: Componente1.SD0, U1.SD0
  N3: Componente1.CMD, U1.CMD
  N4: Componente1.SD1, U1.SD1
  N5: Componente1.RSV#40, U1.RSV#40
  N6: Componente1.VIN#43, U1.Vin
  N7: Componente1.RST, U1.RST
  N8: Componente1.EN, U1.EN
  N9: Componente1.CLK, U1.CLK
  N10: Componente1.SD2, U1.SD2
  N11: Componente1.SD3, U1.SD3
  N12: Componente1.RSV#52, U1.RSV#41
  N13: Componente1.AD0, U1.A0
  N14: Componente1.TX, U1.TX
  N15: Componente1.RX, U1.RX
  N16: Componente1.D8, U1.D8
  N17: Componente1.D7, U1.D7
  N18: Componente1.D6, U1.D6
  N19: Componente1.D5, U1.D5
  N20: Componente1.CB, U1.D4
  N21: Componente1.DA, U1.D3
  N22: Componente1.PWMB, U1.D2
  N23: Componente1.PWMA, U1.D1
  N24: Componente1.D0, U1.D0
  N25: Componente1.A-, M1.pin_2
  N26: Componente1.A+, M1.pin_1
  N27: Componente1.B-, M2.pin_2
  N28: Componente1.B+, M2.pin_1
  N29: Componente1.VM, VCC1.+
  N30: Componente1.GND#101, VCC1.-
  N31: Componente1.VIN#102, VCC2.+
  N32: Componente1.GND#103, VCC2.-

custom parts:
  ESP12E Motor Shield: ESP8266 WiFi Motor Drive Expansion Board For NodeMCU ESP-12E
  NodeMCU V1.0: ESP8266 based NodeMCU
